# Fritzing sketch circuit_omniseek (saved by Fritzing 1.0.1rc)
breadboards: 1

parts:
  HC-SR04_Sensor_1 = HC-SR04 Ultrasonic Distance Sensor
  HC-SR04_Sensor_2 = HC-SR04 Ultrasonic Distance Sensor
  HC-SR04_Sensor_3 = HC-SR04 Ultrasonic Distance Sensor
  VCC2 = 4 x AAA Battery Mount
  Componente5 = SparkFun Motor Driver TB6612FNG (v11) [part_number=ROB-14451]
  Componente6 = SparkFun Motor Driver TB6612FNG (v11) [part_number=ROB-14451]
  U1 = ESP32-38PinWide [part_number=ESP32-38PinWide]
  DC_Mot_Enc1 = DC Motor with two-phase hall-encoder [part_number=VT-E-G25A-06-177E]
  DC_Mot_Enc2 = DC Motor with two-phase hall-encoder [part_number=VT-E-G25A-06-177E]
  DC_Mot_Enc3 = DC Motor with two-phase hall-encoder [part_number=VT-E-G25A-06-177E]

nets:
  VCC: HC-SR04_Sensor_1.VCC, HC-SR04_Sensor_2.VCC, HC-SR04_Sensor_3.VCC, U1.3.3, DC_Mot_Enc1.pin5, DC_Mot_Enc2.pin5, DC_Mot_Enc3.pin5
  N1: HC-SR04_Sensor_1.TRIG, U1.GPIO25
  N2: HC-SR04_Sensor_1.ECHO, U1.GPIO35
  GND: HC-SR04_Sensor_1.GND, HC-SR04_Sensor_2.GND, HC-SR04_Sensor_3.GND, U1.GND, DC_Mot_Enc1.pin2, DC_Mot_Enc2.pin2, DC_Mot_Enc3.pin2
  N3: HC-SR04_Sensor_2.TRIG, U1.GPIO32
  N4: HC-SR04_Sensor_2.ECHO, U1.GPIO39
  N5: HC-SR04_Sensor_3.TRIG, U1.GPIO33
  N6: HC-SR04_Sensor_3.ECHO, U1.GPIO34
  GND_2: VCC2.-, Componente5.GND, Componente6.GND
  N7: VCC2.+, Componente5.VM, Componente6.VM
  N8: Componente5.B01, DC_Mot_Enc1.pin1
  N9: Componente5.B02, DC_Mot_Enc1.pin6
  N10: Componente5.A02, DC_Mot_Enc2.pin1
  N11: Componente5.A01, DC_Mot_Enc2.pin6
  N12: Componente5.PWMA, U1.GPIO13
  N13: Componente5.AIN2, U1.GPIO15
  N14: Componente5.AIN1, U1.GPIO2
  N15: Componente5.STBY, U1.GPIO0
  N16: Componente5.BIN1, U1.GPIO4
  N17: Componente5.BIN2, U1.GPIO16
  N18: Componente5.PWMB, U1.GPIO17
  N19: Componente6.A02, DC_Mot_Enc3.pin1
  N20: Componente6.A01, DC_Mot_Enc3.pin6
  N21: Componente6.PWMA, U1.GPIO26
  N22: Componente6.AIN2, U1.GPIO27
  N23: Componente6.AIN1, U1.GPIO14
  N24: Componente6.STBY, U1.GPIO12
  N25: U1.GPIO5, DC_Mot_Enc2.pin4
  N26: U1.GPIO18, DC_Mot_Enc2.pin3
  N27: U1.GPIO19, DC_Mot_Enc1.pin4
  N28: U1.GPIO21, DC_Mot_Enc1.pin3
  N29: U1.GPIO22, DC_Mot_Enc3.pin4
  N30: U1.GPIO23, DC_Mot_Enc3.pin3

custom parts:
  SparkFun Motor Driver TB6612FNG (v11): The TB6612FNG Motor Driver can control up to two DC motors at a constant current of 1.2A (3.2A peak). Two input signals (IN1 and IN2) can be used to control the motor in one of four function modes: CW, CCW, short-brake and stop. The two motor outputs (A and B) can be separately controlled, and the speed of each motor is controlled via a PWM input signal with a frequency up to 100kHz. The STBY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
  ESP32-38PinWide: Generic 38-Pin ESP32 with wide format (only access to one side of pins on a breadboard) based on Stephen Lilley's HiLetgo ESP-WROOM-32 ESP32 ESP-32S Development Board.
